# Fritzing sketch Receiver (saved by Fritzing 0.9.9b)
breadboards: 1

parts:
  Part1 = Arduino Uno (Rev3) - ICSP
  R1 = Resistor [tolerance=±5% power=0.25 resistance=220 package=THT]
  R2 = Resistor [tolerance=±5% power=0.25 resistance=220 package=THT]
  LED1 = LED - 3mm [color="Red (633nm)" current=0.030 package="3 mm [THT]"]
  J1 = Piezo Speaker
  S1 = Pushbutton [package="[SMD]"]
  Radio_Transmitter1 = NRF24L01+ Breakout Board

nets:
  N1: Part1.5V, S1.Pin_1, S1.Pin_2
  N2: Part1.D8, Radio_Transmitter1.CS
  N3: Part1.D11_PWM/MOSI, Radio_Transmitter1.MOSI
  N4: Part1.D12/MISO, Radio_Transmitter1.MISO
  N5: Part1.D13/SCK, Radio_Transmitter1.SCK
  N6: Part1.D2, LED1.anode
  N7: Part1.D3_PWM, J1.pin2
  N8: Part1.D5_PWM, R1.Pin_1, S1.Pin_3, S1.Pin_4
  N9: Part1.D7, Radio_Transmitter1.CE
  3V3: Part1.3V3, Radio_Transmitter1.VCC
  GND: Part1.GND, R1.Pin_0, R2.Pin_0, J1.pin1, Radio_Transmitter1.GND
  N10: R2.Pin_1, LED1.cathode
