# Fritzing sketch Transmitter (saved by Fritzing 0.9.9b)
breadboards: 1

parts:
  M1 = MAX30102
  LED1 = LED - 5mm [color="Red (633nm)" current=0.030 package="5 mm [THT]"]
  U2 = LCD-16X2 [package=lcd-16x2]
  S2 = Pushbutton [package="[THT]"]
  S3 = Pushbutton [package="[THT]"]
  LED2 = LED - 5mm [color="Red (633nm)" current=0.030 package="5 mm [THT]"]
  R2 = Resistor [tolerance=±5% power=0.25 resistance=220 package=THT]
  R3 = Rotary Potentiometer (Large) [maximum_resistance=100kΩ package=THT]
  R4 = Resistor [tolerance=±5% resistance=220 package="2010 [SMD]"]
  Part2 = Arduino Mega 2560 (Rev3)
  Radio_Transmitter = NRF24L01+ Breakout Board
  R5 = Resistor [tolerance=±5% power=0.25 resistance=220 package=THT]
  R6 = Resistor [tolerance=±5% power=0.25 resistance=220 package=THT]
  R1 = Resistor [tolerance=±5% power=0.25 resistance=220 package=THT]

nets (from the schematic view):
  VIN: M1.VIN, LED1.anode, U2.VDD, S2.Pin_1, S2.Pin_2, S3.Pin_1, S3.Pin_2, LED2.anode, R2.Pin_0, R3.leg1, R4.Pin_1, Part2.D19/RX1, Part2.D18/TX1, Part2.5V, R1.Pin_0
  N1: M1.SCL, Part2.D21/SCL, Part2.SCL
  N2: M1.SDA, Part2.D20/SDA, Part2.SDA
  GND: M1.GND, U2.VSS, U2.R_W, U2.K, R3.leg2, Part2.GND, Radio_Transmitter.GND, R5.Pin_0, R6.Pin_0
  N3: LED1.cathode, R1.Pin_1
  N4: U2.VO, R3.wiper
  N5: U2.RS, Part2.D42
  N6: U2.E, Part2.D43
  N7: U2.DB4, Part2.D34
  N8: U2.DB5, Part2.D35
  N9: U2.DB6, Part2.D36
  N10: U2.DB7, Part2.D37
  N11: U2.A, R4.Pin_0
  N12: S2.Pin_3, S2.Pin_4, R6.Pin_1
  N13: S3.Pin_3, S3.Pin_4, R5.Pin_1
  N14: LED2.cathode, R2.Pin_1
  N15: Part2.D8_PWM, Radio_Transmitter.CS
  3V3: Part2.3V3, Radio_Transmitter.VCC
  N16: Part2.D7_PWM, Radio_Transmitter.CE
  N17: Part2.D50, Radio_Transmitter.MISO
  N18: Part2.D51, Radio_Transmitter.MOSI
  N19: Part2.D52, Radio_Transmitter.SCK

custom parts:
  MAX30102: Oximeter module using the MAX30102 chip. You may wish to read (and check your module) this post on power problems with these modules: https://reedpaper.wordpress.com/2018/08/22/pulse-oximeter-max30100-max30102-how-to-fix-wrong-board/ . As usual, if you want the mounting holes in pcb, you need to drag a hole over the pad in silkscreen to actually drill the hole (by default they are not drilled)
